// Logisim project counter_logic.circ as structural Verilog: 1 circuit, main circuit main
module main (
  input  trigger_C,
  input  trigger_B,
  input  trigger_A,
  input  armed_C,
  input  armed_B,
  input  armed_A,
  output triggered_C,
  output triggered_B,
  output triggered_A,
  output clk_C,
  output clk_B,
  output clk_A
);

  wire and_1_out, and_2_out, armed_p4, clock_1_out, clock_2_out, n7400_1_pin9, n7400_1_pin12, n7408_2_pin9,
       n7408_2_pin12, nand_1_out, nand_2_out, not_1_out, not_2_out, not_3_out, reset_out, trigger_out;

  Clock clock_1 (.out(clock_1_out));
  Button trigger (.out(trigger_out));
  // Switch armed: pin names not known; wires that end beside it: trigger_C, armed_C, 1'b1, armed_p4
  Button reset (.out(reset_out));
  not not_1 (not_1_out, trigger_B);
  not not_2 (not_2_out, trigger_A);
  Clock clock_2 (.out(clock_2_out));
  Pull_Resistor pull_resistor_1 (.node(armed_p4));
  not not_3 (not_3_out, trigger_out);
  nand nand_1 (nand_1_out, and_1_out, armed_p4);
  nand nand_2 (nand_2_out, not_3_out, nand_1_out);
  _7408 u_7408_1 (
    .pin13(clock_2_out), .pin12(triggered_A), .pin11(clk_A), .pin10(clock_2_out), .pin9(triggered_B),
    .pin8(clk_B));  // open: pin1, pin2, pin3, pin4, pin5, pin6
  and and_1 (and_1_out, nand_2_out, armed_p4);
  and and_2 (and_2_out, clock_1_out, and_1_out);
  _7408 u_7408_2 (
    .pin13(armed_A), .pin12(n7408_2_pin12), .pin11(triggered_A), .pin10(armed_B), .pin9(n7408_2_pin9),
    .pin8(triggered_B));  // open: pin1, pin2, pin3, pin4, pin5, pin6
  Counter counter_1 (.clr(reset_out), .clk(and_2_out));  // open: load, up, count, D, carry, Q
  _7400 u_7400_1 (
    .pin13(not_2_out), .pin12(n7400_1_pin12), .pin11(n7408_2_pin12), .pin10(not_1_out), .pin9(n7400_1_pin9),
    .pin8(n7408_2_pin9));  // open: pin1, pin2, pin3, pin4, pin5, pin6
  _7400 u_7400_2 (
    .pin13(n7408_2_pin12), .pin12(armed_A), .pin11(n7400_1_pin12), .pin10(n7408_2_pin9), .pin9(armed_B),
    .pin8(n7400_1_pin9));  // open: pin1, pin2, pin3, pin4, pin5, pin6
endmodule
